# Fritzing sketch software_implementation (saved by Fritzing 0.9.3b)
breadboards: 1

parts:
  LED1 = LED - 5mm [color="Red (633nm)" package="5 mm [THT]"]
  LED2 = LED - 5mm [color="Red (633nm)" package="5 mm [THT]"]
  R1 = Resistor [tolerance=±5% resistance=220 package=THT]
  R2 = Resistor [tolerance=±5% resistance=220 package=THT]
  SW1 = ENCODER_RGB_CA [package=encoder_led_3]
  IC1 = IC, DIP package, 56 pins [chip_label="atmega4809 curiosity nano"]

nets:
  N1: LED1.cathode, R1.Pin_1
  N2: LED1.anode, IC1.pin31
  N3: LED2.cathode, R2.Pin_1
  N4: LED2.anode, IC1.pin30
  N5: R1.Pin_0, R2.Pin_0
  N6: SW1.-B, IC1.pin52
  N7: SW1.+, IC1.pin55, IC1.pin56
  N8: SW1.B, IC1.pin26
  N9: SW1.C, IC1.pin25

notes:
  These go to serial adapter RX and TX
  For rotary encoder: Blue is CLK and Green is DT
  External Power source. I used the Serial adapter to get 5V. VOFF NEEDS to be grounded for this to work
